# Fritzing sketch StupedBaxPCB (saved by Fritzing 0.9.3b)
circuit board: 5.01198cm x 6.86045cm
perfboards: 1

parts:
  U1 = atmega328 [package=dip]
  part = Toggle Switch [package=THT]
  R1 = Resistor [tolerance=±5% resistance=680 package=THT]
  6V = Battery
  Q1 = Basic FET P-Channel [package="TO220 [THT]"]
  R2 = Resistor [tolerance=±5% resistance=100 package=THT]
  LID = Basic Servo
  D1 = Rectifier Diode [part_number=1N4001 package="300 mil [THT]"]
  R3 = Resistor [tolerance=±5% resistance=100 package=THT]
  ARM = Basic Servo

nets:
  N1: U1.D2, part.COM
  GND: U1.VCC, U1.AVCC, 6V.+, Q1.source, R2.Pin_1
  N2: U1.D8, R3.Pin_1
  VCC: U1.D9_(PWM), Q1.drain, LID.vcc, ARM.vcc, ARM.pulse
  N3: U1.D10_(PWM), LID.pulse
  GND_2: U1.GND#21, R1.Pin_0, 6V.-, LID.gnd, ARM.gnd
  N4: part.L1, R1.Pin_1
  N5: Q1.gate, R2.Pin_0, D1.anode
  N6: D1.cathode, R3.Pin_0
